# Fritzing sketch clock_oclock_v2 (saved by Fritzing 0.9.3b)
circuit board: 8.46667cm x 5.64444cm
breadboards: 1

parts:
  part = Arduino Pro Mini (5V)
  Hall_Sensor = mystery part, 3 pins [chip_label="Flat Side"]
  Motor_Connectors_(B_A_V+_GND) = screw terminal, 4 pins  # not connected
  Back_Button = Pushbutton [package="[THT]"]
  FWD_Button = Pushbutton [package="[THT]"]
  R1 = Resistor [tolerance=±5% resistance=1k package="1206 [SMD]"]
  R2 = Resistor [tolerance=±5% resistance=1k package="1206 [SMD]"]
  RTC = Adafruit DS1307 RTC Breakout
  Polulu_Motor_Driver = mystery part, 8 pins [chip_label="Polulu MD05A"]
  R3 = Resistor [tolerance=±5% resistance=10k package="1206 [SMD]"]
  Motor_with_Encoder = mystery part, 6 pins

nets:
  VCC: part.VCC, Hall_Sensor.pin3, R1.Pin_1, R2.Pin_1, RTC.VCC, R3.Pin_0, Motor_with_Encoder.pin4
  GND: part.GND, Hall_Sensor.pin2, Back_Button.Pin_1, Back_Button.Pin_2, FWD_Button.Pin_1, FWD_Button.Pin_2, RTC.GND, Polulu_Motor_Driver.pin8, Motor_with_Encoder.pin3
  N1: part.A4, RTC.SDA
  N2: part.A5, RTC.SCL
  N3: part.A0, Hall_Sensor.pin1, R3.Pin_1
  N4: part.D9, Back_Button.Pin_3, Back_Button.Pin_4
  N5: part.D8, FWD_Button.Pin_3, FWD_Button.Pin_4
  N6: part.D7, Polulu_Motor_Driver.pin3
  N7: part.D6, Polulu_Motor_Driver.pin6
  N8: part.D5, Polulu_Motor_Driver.pin1
  N9: part.D4, Polulu_Motor_Driver.pin4
  N10: part.D3, R2.Pin_0, Motor_with_Encoder.pin1
  N11: part.D2, R1.Pin_0, Motor_with_Encoder.pin2

custom parts:
  Adafruit DS1307 RTC Breakout: This is a great battery-backed real time clock (RTC) that allows your microcontroller project to keep track of time even if it is reprogrammed, or if the power is lost. Perfect for datalogging, clock-building, time stamping, timers and alarms, etc. The DS1307 is the most popular RTC - but it requires 5V power to work (although we've used it with 5V power and 3.3V logic successfully) PCB &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
